# Fritzing sketch water-filter (saved by Fritzing 0.9.3b)

parts:
  Part3 = Arduino Nano (Rev3.0)
  LED2 = RGB LED (com. cathode, rgb) [package="5 mm [THT]"]
  Part4 = HX711 Weighing Sensor Module
  Load_Cell1 = Load Cell - Red/white/black/green

nets:
  GND: Part3.GND, LED2.common_cathode, Part4.GND
  N1: Part3.D9, LED2.blue_anode
  N2: Part3.D10, LED2.green_anode
  N3: Part3.D11/MOSI, LED2.red_anode
  5V: Part3.5V, Part4.VCC
  N4: Part3.A1, Part4.CK/TX
  N5: Part3.A0, Part4.DO/RX
  N6: Part4.E+, Load_Cell1.wire1
  N7: Part4.E-, Load_Cell1.wire3
  N8: Part4.A+, Load_Cell1.wire4
  N9: Part4.A-, Load_Cell1.wire2

custom parts:
  Load Cell - Red/white/black/green: A rectangle load cell/weighting pressure Sensor with four wires - Red, white, black, green. Normally corresponding with E+, E-, A+, A- respectively.
